# Fritzing sketch mqtts_client (saved by Fritzing 0.7.11b)
breadboards: 1

parts:
  Arduino1 = Arduino  # not connected
  Q1 = NPN-Transistor [package="TO92 [THT]"]
  P1 = S1133 Si Photodiode [package="8mm Ceramic [THT]"]
  LED1 = yellow smd LED [package="1206 [SMD]"]
  LED2 = yellow smd LED [package="1206 [SMD]"]
  LED3 = yellow smd LED [package="1206 [SMD]"]
  LED4 = smd LED [color="Red (633nm)" package="0805 [SMD]"]
  LED5 = smd LED [color="Red (633nm)" package="0805 [SMD]"]
  LED6 = smd LED [color="Red (633nm)" package="0805 [SMD]"]
  LED7 = smd LED [color="Red (633nm)" package="0805 [SMD]"]
  LED8 = yellow smd LED [package="1206 [SMD]"]
  R1 = Resistor [tolerance=±5% resistance=220 package="0603 [SMD]"]
  R2 = Resistor [tolerance=±5% resistance=220 package="0603 [SMD]"]  # not connected
  R4 = Resistor [tolerance=±5% resistance=220 package="0603 [SMD]"]
  R5 = Resistor [tolerance=±5% resistance=220 package="0603 [SMD]"]
  R6 = Resistor [tolerance=±5% resistance=220 package="0603 [SMD]"]
  R7 = Resistor [tolerance=±5% resistance=220 package="0603 [SMD]"]
  R8 = Resistor [tolerance=±5% resistance=220 package="0603 [SMD]"]
  R9 = Resistor [tolerance=±5% resistance=220 package="0603 [SMD]"]
  R10 = 10k Ω Resistor [package=THT]
  R11 = Resistor [tolerance=±5% resistance=220 package="0603 [SMD]"]
  U1 = XBee  # not connected
  Part1 = Arduino XBee Shield

nets:
  N1: Q1.E, P1.cathode, Part1.5V
  N2: Q1.B, Part1.A1
  N3: Q1.C, R1.Pin_1, R4.Pin_1, R5.Pin_1, R6.Pin_1, R7.Pin_1, R8.Pin_1, R9.Pin_1, R10.Pin_1, R11.Pin_1, Part1.GND
  N4: P1.anode, R10.Pin_0, Part1.A0
  N5: LED1.cathode, R1.Pin_0
  N6: LED1.anode, Part1.D7
  N7: LED2.cathode, R11.Pin_0
  N8: LED2.anode, Part1.D8
  N9: LED3.cathode, R4.Pin_0
  N10: LED3.anode, Part1.D9
  N11: LED4.cathode, R5.Pin_0
  N12: LED4.anode, Part1.D10
  N13: LED5.cathode, R6.Pin_0
  N14: LED5.anode, Part1.D11
  N15: LED6.cathode, R7.Pin_0
  N16: LED6.anode, Part1.D12
  N17: LED7.cathode, R9.Pin_0
  N18: LED7.anode, Part1.D13
  N19: LED8.cathode, R8.Pin_0
  N20: LED8.anode, Part1.D6

notes:
  send packet
  ACK
  receive packet
  connected to GW
  connected to broker
  register all topics
  error
  controled led
  photoresistor
  temperature sensor
