# Fritzing sketch simple_mqtts_client (saved by Fritzing 0.7.11b)
breadboards: 1

parts:
  Arduino1 = Arduino  # not connected
  P1 = S1133 Si Photodiode [package="8mm Ceramic [THT]"]
  LED5 = smd LED [color="Red (633nm)" package="0805 [SMD]"]
  LED8 = yellow smd LED [package="1206 [SMD]"]
  R2 = Resistor [tolerance=±5% resistance=220 package="0603 [SMD]"]  # not connected
  R6 = Resistor [tolerance=±5% resistance=220 package="0603 [SMD]"]
  R7 = Resistor [tolerance=±5% resistance=220 package="0603 [SMD]"]
  R10 = 10k Ω Resistor [package=THT]
  Part1 = Arduino XBee Shield
  U1 = XBee  # not connected

nets:
  N1: P1.cathode, Part1.5V
  N2: P1.anode, R10.Pin_0, Part1.A0
  N3: LED5.cathode, R6.Pin_0
  N4: LED5.anode, Part1.D11
  N5: LED8.cathode, R7.Pin_0
  N6: LED8.anode, Part1.D12
  N7: R6.Pin_1, R7.Pin_1, R10.Pin_1, Part1.GND

notes:
  active
  controled led
  photoresistor
